# Fritzing sketch Schema Proiect (saved by Fritzing 0.9.3b)
breadboards: 1

parts:
  Raspberry_Pi_1 = Raspberry Pi 3 [part_number=RPI-3-V1.2]
  Q1 = TRANSISTOR_NPN [package=sot89]
  L1 = Solenoid
  S1 = Pushbutton [package="[THT]"]
  R1 = Resistor [tolerance=±5% resistance=220 package=THT]
  VCC1 = Battery block 9V

nets:
  N1: Raspberry_Pi_1.GIPO19, S1.Pin_1, S1.Pin_2
  N2: Raspberry_Pi_1.GND, L1.pin1, VCC1.-
  N3: Raspberry_Pi_1.GIPO21, Q1.B
  N4: Q1.C, R1.Pin_0, VCC1.+
  N5: Q1.E, L1.pin2
  N6: S1.Pin_3, S1.Pin_4, R1.Pin_1
